// Logisim project calculatorCPU.circ as structural Verilog: 18 circuits, main circuit main
module main (
  input  Clear
);

  wire _0_out, _1_out, _2_out, _3_out, _4_out, _5_out, _6_out, _7_out, _8_out, _9_out, button_2_out,
       button_3_out, button_4_out, button_5_out, button_out, C_out, clock_1_out, keypad_controller_1_write;
  wire [2:0] lcd_controller_1__7_segment_3_2, lcd_controller_1__7_segment_4_2,
       lcd_controller_1__7_segment_5_2, lcd_controller_1__7_segment_6_2, lcd_controller_1__7_segment_7_2,
       lcd_controller_1__7_segment_8_2, lcd_controller_1__7_segment_9_2, lcd_controller_1_minus_2;
  wire [3:0] lcd_controller_1__7_segment_3, lcd_controller_1__7_segment_4, lcd_controller_1__7_segment_5,
       lcd_controller_1__7_segment_6, lcd_controller_1__7_segment_7, lcd_controller_1__7_segment_8,
       lcd_controller_1__7_segment_9, lcd_controller_1_minus;
  wire [6:0] lcd_controller_1__7_segment_0, lcd_controller_1__7_segment_1, lcd_controller_1__7_segment_2;
  wire [31:0] cpu_to_do_1_t8tolcd, cpu_to_do_1_t9tokeypad, keypad_controller_1_output;

  CPU__TO_DO cpu_to_do_1 (
    .Clock(clock_1_out), .Clear(Clear), .WriteSig(keypad_controller_1_write),
    .WriteTo_t9(keypad_controller_1_output), .t8ToLCD(cpu_to_do_1_t8tolcd),
    .t9ToKeypad(cpu_to_do_1_t9tokeypad));
  Clock clock_1 (.out(clock_1_out));
  _7_Segment_Display u_7_segment_display_1 (
    .g(lcd_controller_1__7_segment_9[0]), .f(lcd_controller_1__7_segment_9[1]),
    .a(lcd_controller_1__7_segment_9[2]), .b(lcd_controller_1__7_segment_9[3]),
    .e(lcd_controller_1__7_segment_9_2[0]), .d(lcd_controller_1__7_segment_9_2[1]),
    .c(lcd_controller_1__7_segment_9_2[2]));  // open: dp
  _7_Segment_Display u_7_segment_display_2 (
    .g(lcd_controller_1_minus[0]), .f(lcd_controller_1_minus[1]), .a(lcd_controller_1_minus[2]),
    .b(lcd_controller_1_minus[3]), .e(lcd_controller_1_minus_2[0]), .d(lcd_controller_1_minus_2[1]),
    .c(lcd_controller_1_minus_2[2]));  // open: dp
  LCD_Controller lcd_controller_1 (
    .From__t8(cpu_to_do_1_t8tolcd), .Minus({lcd_controller_1_minus_2, lcd_controller_1_minus}),
    ._7_Segment_9({lcd_controller_1__7_segment_9_2, lcd_controller_1__7_segment_9}),
    ._7_Segment_8({lcd_controller_1__7_segment_8_2, lcd_controller_1__7_segment_8}),
    ._7_Segment_7({lcd_controller_1__7_segment_7_2, lcd_controller_1__7_segment_7}),
    ._7_Segment_6({lcd_controller_1__7_segment_6_2, lcd_controller_1__7_segment_6}),
    ._7_Segment_5({lcd_controller_1__7_segment_5_2, lcd_controller_1__7_segment_5}),
    ._7_Segment_4({lcd_controller_1__7_segment_4_2, lcd_controller_1__7_segment_4}),
    ._7_Segment_3({lcd_controller_1__7_segment_3_2, lcd_controller_1__7_segment_3}),
    ._7_Segment_2(lcd_controller_1__7_segment_2), ._7_Segment_1(lcd_controller_1__7_segment_1),
    ._7_Segment_0(lcd_controller_1__7_segment_0));
  Keypad_Controller keypad_controller_1 (
    .C(C_out), .in_2(button_out), .in_3(button_5_out), .in_4(button_4_out), .in_5(button_3_out),
    .in_6(button_2_out), ._9(_9_out), ._8(_8_out), ._7(_7_out), ._6(_6_out), ._5(_5_out), ._4(_4_out),
    ._3(_3_out), ._2(_2_out), ._1(_1_out), ._0(_0_out), .From__t9(cpu_to_do_1_t9tokeypad),
    .Write(keypad_controller_1_write), .Output(keypad_controller_1_output));
  _7_Segment_Display u_7_segment_display_3 (
    .g(lcd_controller_1__7_segment_7[0]), .f(lcd_controller_1__7_segment_7[1]),
    .a(lcd_controller_1__7_segment_7[2]), .b(lcd_controller_1__7_segment_7[3]),
    .e(lcd_controller_1__7_segment_7_2[0]), .d(lcd_controller_1__7_segment_7_2[1]),
    .c(lcd_controller_1__7_segment_7_2[2]));  // open: dp
  _7_Segment_Display u_7_segment_display_4 (
    .g(lcd_controller_1__7_segment_8[0]), .f(lcd_controller_1__7_segment_8[1]),
    .a(lcd_controller_1__7_segment_8[2]), .b(lcd_controller_1__7_segment_8[3]),
    .e(lcd_controller_1__7_segment_8_2[0]), .d(lcd_controller_1__7_segment_8_2[1]),
    .c(lcd_controller_1__7_segment_8_2[2]));  // open: dp
  _7_Segment_Display u_7_segment_display_5 (
    .g(lcd_controller_1__7_segment_5[0]), .f(lcd_controller_1__7_segment_5[1]),
    .a(lcd_controller_1__7_segment_5[2]), .b(lcd_controller_1__7_segment_5[3]),
    .e(lcd_controller_1__7_segment_5_2[0]), .d(lcd_controller_1__7_segment_5_2[1]),
    .c(lcd_controller_1__7_segment_5_2[2]));  // open: dp
  _7_Segment_Display u_7_segment_display_6 (
    .g(lcd_controller_1__7_segment_6[0]), .f(lcd_controller_1__7_segment_6[1]),
    .a(lcd_controller_1__7_segment_6[2]), .b(lcd_controller_1__7_segment_6[3]),
    .e(lcd_controller_1__7_segment_6_2[0]), .d(lcd_controller_1__7_segment_6_2[1]),
    .c(lcd_controller_1__7_segment_6_2[2]));  // open: dp
  Button _7 (.out(_7_out));
  Button _4 (.out(_4_out));
  Button _1 (.out(_1_out));
  Button _0 (.out(_0_out));
  _7_Segment_Display u_7_segment_display_7 (
    .g(lcd_controller_1__7_segment_3[0]), .f(lcd_controller_1__7_segment_3[1]),
    .a(lcd_controller_1__7_segment_3[2]), .b(lcd_controller_1__7_segment_3[3]),
    .e(lcd_controller_1__7_segment_3_2[0]), .d(lcd_controller_1__7_segment_3_2[1]),
    .c(lcd_controller_1__7_segment_3_2[2]));  // open: dp
  _7_Segment_Display u_7_segment_display_8 (
    .g(lcd_controller_1__7_segment_4[0]), .f(lcd_controller_1__7_segment_4[1]),
    .a(lcd_controller_1__7_segment_4[2]), .b(lcd_controller_1__7_segment_4[3]),
    .e(lcd_controller_1__7_segment_4_2[0]), .d(lcd_controller_1__7_segment_4_2[1]),
    .c(lcd_controller_1__7_segment_4_2[2]));  // open: dp
  Button _8 (.out(_8_out));
  Button _5 (.out(_5_out));
  Button _2 (.out(_2_out));
  Button C (.out(C_out));
  _7_Segment_Display u_7_segment_display_9 (
    .g(lcd_controller_1__7_segment_2[0]), .f(lcd_controller_1__7_segment_2[1]),
    .a(lcd_controller_1__7_segment_2[2]), .b(lcd_controller_1__7_segment_2[3]),
    .e(lcd_controller_1__7_segment_2[4]), .d(lcd_controller_1__7_segment_2[5]),
    .c(lcd_controller_1__7_segment_2[6]));  // open: dp
  _7_Segment_Display u_7_segment_display_10 (
    .g(lcd_controller_1__7_segment_1[0]), .f(lcd_controller_1__7_segment_1[1]),
    .a(lcd_controller_1__7_segment_1[2]), .b(lcd_controller_1__7_segment_1[3]),
    .e(lcd_controller_1__7_segment_1[4]), .d(lcd_controller_1__7_segment_1[5]),
    .c(lcd_controller_1__7_segment_1[6]));  // open: dp
  Button _9 (.out(_9_out));
  Button _6 (.out(_6_out));
  Button _3 (.out(_3_out));
  Button button (.out(button_out));
  _7_Segment_Display u_7_segment_display_11 (
    .g(lcd_controller_1__7_segment_0[0]), .f(lcd_controller_1__7_segment_0[1]),
    .a(lcd_controller_1__7_segment_0[2]), .b(lcd_controller_1__7_segment_0[3]),
    .e(lcd_controller_1__7_segment_0[4]), .d(lcd_controller_1__7_segment_0[5]),
    .c(lcd_controller_1__7_segment_0[6]));  // open: dp
  Button button_2 (.out(button_2_out));
  Button button_3 (.out(button_3_out));
  Button button_4 (.out(button_4_out));
  Button button_5 (.out(button_5_out));

  // Notes on the sheet:
  //   From $t8
  //   From $t9
  //   Write Data to $t9
  //   Write Signal for $t9
endmodule

module LCD_Controller (
  input  [31:0] From__t8,
  output [6:0] Minus,
  output [6:0] _7_Segment_9,
  output [6:0] _7_Segment_8,
  output [6:0] _7_Segment_7,
  output [6:0] _7_Segment_6,
  output [6:0] _7_Segment_5,
  output [6:0] _7_Segment_4,
  output [6:0] _7_Segment_3,
  output [6:0] _7_Segment_2,
  output [6:0] _7_Segment_1,
  output [6:0] _7_Segment_0
);

  wire [3:0] binarytobcd_1_bcd0, binarytobcd_1_bcd1, binarytobcd_1_bcd2, binarytobcd_1_bcd3,
       binarytobcd_1_bcd4, binarytobcd_1_bcd5, binarytobcd_1_bcd6, binarytobcd_1_bcd7, binarytobcd_1_bcd8,
       binarytobcd_1_bcd9;

  BinaryToBCD binarytobcd_1 (
    .Input(From__t8), .Minus(Minus[0]), .BCD9(binarytobcd_1_bcd9), .BCD8(binarytobcd_1_bcd8),
    .BCD7(binarytobcd_1_bcd7), .BCD6(binarytobcd_1_bcd6), .BCD5(binarytobcd_1_bcd5),
    .BCD4(binarytobcd_1_bcd4), .BCD3(binarytobcd_1_bcd3), .BCD2(binarytobcd_1_bcd2),
    .BCD1(binarytobcd_1_bcd1), .BCD0(binarytobcd_1_bcd0));
  _7_Segment_Controller u_7_segment_controller_1 (.BCD(binarytobcd_1_bcd9), .out_2(_7_Segment_9));
  _7_Segment_Controller u_7_segment_controller_2 (.BCD(binarytobcd_1_bcd8), .out_2(_7_Segment_8));
  _7_Segment_Controller u_7_segment_controller_3 (.BCD(binarytobcd_1_bcd7), .out_2(_7_Segment_7));
  _7_Segment_Controller u_7_segment_controller_4 (.BCD(binarytobcd_1_bcd6), .out_2(_7_Segment_6));
  _7_Segment_Controller u_7_segment_controller_5 (.BCD(binarytobcd_1_bcd5), .out_2(_7_Segment_5));
  _7_Segment_Controller u_7_segment_controller_6 (.BCD(binarytobcd_1_bcd4), .out_2(_7_Segment_4));
  _7_Segment_Controller u_7_segment_controller_7 (.BCD(binarytobcd_1_bcd3), .out_2(_7_Segment_3));
  _7_Segment_Controller u_7_segment_controller_8 (.BCD(binarytobcd_1_bcd2), .out_2(_7_Segment_2));
  _7_Segment_Controller u_7_segment_controller_9 (.BCD(binarytobcd_1_bcd1), .out_2(_7_Segment_1));
  _7_Segment_Controller u_7_segment_controller_10 (.BCD(binarytobcd_1_bcd0), .out_2(_7_Segment_0));

  assign Minus[6:1] = {6{1'b0}};
endmodule

module _7_Segment_Controller (
  input  [3:0] BCD,
  output [6:0] out_2
);

  wire and_1_out, and_2_out, and_3_out, and_4_out, and_5_out, and_6_out, and_7_out, and_8_out, and_9_out,
       and_10_out, and_11_out, and_12_out, and_13_out, and_14_out, and_15_out, and_16_out, not_1_out,
       not_2_out, not_3_out, not_4_out, not_5_out, not_6_out, not_7_out, not_8_out, not_9_out, not_10_out,
       not_11_out, not_12_out, not_13_out, not_14_out, not_15_out, not_16_out, not_17_out, not_18_out,
       not_19_out, not_20_out, not_21_out;

  not not_1 (not_1_out, BCD[2]);
  not not_2 (not_2_out, BCD[0]);
  not not_3 (not_3_out, BCD[1]);
  not not_4 (not_4_out, BCD[1]);
  not not_5 (not_5_out, BCD[0]);
  not not_6 (not_6_out, BCD[1]);
  not not_7 (not_7_out, BCD[0]);
  not not_8 (not_8_out, BCD[2]);
  not not_9 (not_9_out, BCD[0]);
  not not_10 (not_10_out, BCD[1]);
  not not_11 (not_11_out, BCD[0]);
  not not_12 (not_12_out, BCD[2]);
  not not_13 (not_13_out, BCD[0]);
  not not_14 (not_14_out, BCD[0]);
  not not_15 (not_15_out, BCD[2]);
  not not_16 (not_16_out, BCD[0]);
  not not_17 (not_17_out, BCD[2]);
  not not_18 (not_18_out, BCD[0]);
  not not_19 (not_19_out, BCD[1]);
  not not_20 (not_20_out, BCD[1]);
  and and_1 (and_1_out, not_1_out, BCD[1]);
  and and_2 (and_2_out, BCD[1], not_2_out);
  and and_3 (and_3_out, BCD[2], not_3_out);
  and and_4 (and_4_out, not_4_out, not_5_out);
  and and_5 (and_5_out, BCD[2], not_6_out);
  and and_6 (and_6_out, BCD[2], not_7_out);
  and and_7 (and_7_out, not_8_out, not_9_out);
  and and_8 (and_8_out, BCD[2], BCD[0]);
  not not_21 (not_21_out, BCD[2]);
  and and_9 (and_9_out, not_10_out, not_11_out);
  and and_10 (and_10_out, BCD[1], BCD[0]);
  and and_11 (and_11_out, not_12_out, not_13_out);
  and and_12 (and_12_out, BCD[1], not_14_out);
  and and_13 (and_13_out, not_15_out, not_16_out);
  and and_14 (and_14_out, not_17_out, BCD[1]);
  and and_15 (and_15_out, BCD[1], not_18_out);
  and and_16 (and_16_out, BCD[2], not_19_out, BCD[0]);
  or or_1 (out_2[6], not_20_out, BCD[0], BCD[2]);
  or or_2 (out_2[0], and_1_out, and_2_out, and_3_out, BCD[3]);
  or or_3 (out_2[1], and_4_out, and_5_out, and_6_out, BCD[3]);
  or or_4 (out_2[2], and_7_out, BCD[1], and_8_out, BCD[3]);
  or or_5 (out_2[3], not_21_out, and_9_out, and_10_out);
  or or_6 (out_2[4], and_11_out, and_12_out);
  or or_7 (out_2[5], and_13_out, and_14_out, and_15_out, and_16_out);
endmodule

module BinaryToBCD (
  input  [31:0] Input,
  output Minus,
  output [3:0] BCD9,
  output [3:0] BCD8,
  output [3:0] BCD7,
  output [3:0] BCD6,
  output [3:0] BCD5,
  output [3:0] BCD4,
  output [3:0] BCD3,
  output [3:0] BCD2,
  output [3:0] BCD1,
  output [3:0] BCD0
);

  wire [27:0] subtractor_1_out, subtractor_2_out, subtractor_3_out, subtractor_4_out, subtractor_5_out,
       subtractor_6_out, subtractor_7_out, subtractor_8_out, subtractor_9_out;
  wire [31:0] adder_1_out, divider_1_out, divider_2_out, divider_3_out, divider_4_out, divider_5_out,
       divider_6_out, divider_7_out, divider_8_out, multiplexer_1_out, multiplier_1_out, multiplier_2_out,
       multiplier_3_out, multiplier_4_out, multiplier_5_out, multiplier_6_out, multiplier_7_out,
       multiplier_8_out, multiplier_9_out, not_1_out;
  wire [31:4] divider_9_out;

  assign not_1_out = ~Input;  // NOT_Gate not_1, 32 bits wide
  Adder #(.width(32)) adder_1 (.a(not_1_out), .b(32'h1), .out(adder_1_out));  // open: cin, cout
  Multiplexer #(.width(32)) multiplexer_1 (
    .in0(Input), .in1(adder_1_out), .out(multiplexer_1_out), .sel(Input[31]));  // open: en
  Subtractor #(.width(32)) subtractor_1 (
    .a(multiplexer_1_out), .b(multiplier_1_out), .out({subtractor_1_out, BCD0}));  // open: bin, bout
  Multiplier #(.width(32)) multiplier_1 (.a(divider_1_out), .b(32'ha), .out(multiplier_1_out));  // open: cin, cout
  Divider #(.width(32)) divider_1 (.a(multiplexer_1_out), .b(32'ha), .out(divider_1_out));  // open: upper, rem
  Subtractor #(.width(32)) subtractor_2 (
    .a(divider_1_out), .b(multiplier_2_out), .out({subtractor_2_out, BCD1}));  // open: bin, bout
  Multiplier #(.width(32)) multiplier_2 (.a(divider_2_out), .b(32'ha), .out(multiplier_2_out));  // open: cin, cout
  Divider #(.width(32)) divider_2 (.a(divider_1_out), .b(32'ha), .out(divider_2_out));  // open: upper, rem
  Subtractor #(.width(32)) subtractor_3 (
    .a(divider_2_out), .b(multiplier_3_out), .out({subtractor_3_out, BCD2}));  // open: bin, bout
  Multiplier #(.width(32)) multiplier_3 (.a(divider_3_out), .b(32'ha), .out(multiplier_3_out));  // open: cin, cout
  Divider #(.width(32)) divider_3 (.a(divider_2_out), .b(32'ha), .out(divider_3_out));  // open: upper, rem
  Subtractor #(.width(32)) subtractor_4 (
    .a(divider_3_out), .b(multiplier_4_out), .out({subtractor_4_out, BCD3}));  // open: bin, bout
  Multiplier #(.width(32)) multiplier_4 (.a(divider_4_out), .b(32'ha), .out(multiplier_4_out));  // open: cin, cout
  Divider #(.width(32)) divider_4 (.a(divider_3_out), .b(32'ha), .out(divider_4_out));  // open: upper, rem
  Subtractor #(.width(32)) subtractor_5 (
    .a(divider_4_out), .b(multiplier_5_out), .out({subtractor_5_out, BCD4}));  // open: bin, bout
  Multiplier #(.width(32)) multiplier_5 (.a(divider_5_out), .b(32'ha), .out(multiplier_5_out));  // open: cin, cout
  Divider #(.width(32)) divider_5 (.a(divider_4_out), .b(32'ha), .out(divider_5_out));  // open: upper, rem
  Subtractor #(.width(32)) subtractor_6 (
    .a(divider_5_out), .b(multiplier_6_out), .out({subtractor_6_out, BCD5}));  // open: bin, bout
  Multiplier #(.width(32)) multiplier_6 (.a(divider_6_out), .b(32'ha), .out(multiplier_6_out));  // open: cin, cout
  Divider #(.width(32)) divider_6 (.a(divider_5_out), .b(32'ha), .out(divider_6_out));  // open: upper, rem
  Subtractor #(.width(32)) subtractor_7 (
    .a(divider_6_out), .b(multiplier_7_out), .out({subtractor_7_out, BCD6}));  // open: bin, bout
  Multiplier #(.width(32)) multiplier_7 (.a(divider_7_out), .b(32'ha), .out(multiplier_7_out));  // open: cin, cout
  Divider #(.width(32)) divider_7 (.a(divider_6_out), .b(32'ha), .out(divider_7_out));  // open: upper, rem
  Subtractor #(.width(32)) subtractor_8 (
    .a(divider_7_out), .b(multiplier_8_out), .out({subtractor_8_out, BCD7}));  // open: bin, bout
  Multiplier #(.width(32)) multiplier_8 (.a(divider_8_out), .b(32'ha), .out(multiplier_8_out));  // open: cin, cout
  Divider #(.width(32)) divider_8 (.a(divider_7_out), .b(32'ha), .out(divider_8_out));  // open: upper, rem
  Subtractor #(.width(32)) subtractor_9 (
    .a(divider_8_out), .b(multiplier_9_out), .out({subtractor_9_out, BCD8}));  // open: bin, bout
  Multiplier #(.width(32)) multiplier_9 (
    .a({divider_9_out, BCD9}), .b(32'ha), .out(multiplier_9_out));  // open: cin, cout
  Divider #(.width(32)) divider_9 (.a(divider_8_out), .b(32'ha), .out({divider_9_out, BCD9}));  // open: upper, rem

  assign Minus = Input[31];
endmodule

module Keypad_Controller (
  input  C,
  input  in_2,
  input  in_3,
  input  in_4,
  input  in_5,
  input  in_6,
  input  _9,
  input  _8,
  input  _7,
  input  _6,
  input  _5,
  input  _4,
  input  _3,
  input  _2,
  input  _1,
  input  _0,
  input  [31:0] From__t9,
  output Write,
  output [31:0] Output
);

  wire iszero_1_out_2, iszero_2_out_2;
  wire [3:0] or_4_out;
  wire [15:0] and_1_out;

  and and_1 (and_1_out[0], C, iszero_1_out_2);
  and and_2 (and_1_out[1], in_2, iszero_1_out_2);
  and and_3 (and_1_out[2], in_3, iszero_1_out_2);
  and and_4 (and_1_out[3], in_4, iszero_1_out_2);
  and and_5 (and_1_out[4], in_5, iszero_1_out_2);
  and and_6 (and_1_out[5], in_6, iszero_1_out_2);
  and and_7 (and_1_out[6], _9, iszero_1_out_2);
  and and_8 (and_1_out[7], _8, iszero_1_out_2);
  and and_9 (and_1_out[8], _7, iszero_1_out_2);
  and and_10 (and_1_out[9], _6, iszero_1_out_2);
  and and_11 (and_1_out[10], _5, iszero_1_out_2);
  and and_12 (and_1_out[11], _4, iszero_1_out_2);
  and and_13 (and_1_out[12], _3, iszero_1_out_2);
  and and_14 (and_1_out[13], _2, iszero_1_out_2);
  and and_15 (and_1_out[14], _1, iszero_1_out_2);
  and and_16 (and_1_out[15], _0, iszero_1_out_2);
  isZero iszero_1 (.Input(From__t9), .out_2(iszero_1_out_2));
  or or_1 (or_4_out[3], and_1_out[0], and_1_out[1], and_1_out[2], and_1_out[3], and_1_out[4], and_1_out[5], and_1_out[6], and_1_out[7]);
  or or_2 (or_4_out[2], and_1_out[8], and_1_out[9], and_1_out[10], and_1_out[11], and_1_out[0], and_1_out[1], and_1_out[2], and_1_out[3]);
  or or_3 (or_4_out[1], and_1_out[12], and_1_out[13], and_1_out[9], and_1_out[8], and_1_out[5], and_1_out[4], and_1_out[1], and_1_out[0]);
  or or_4 (or_4_out[0], and_1_out[12], and_1_out[14], and_1_out[10], and_1_out[8], and_1_out[6], and_1_out[4], and_1_out[2], and_1_out[0]);
  isZero iszero_2 (.Input({{16{1'b0}}, and_1_out}), .out_2(iszero_2_out_2));
  not not_1 (Write, iszero_2_out_2);
  assign Output = Write ? {28'h8000000, or_4_out} : 32'bz;  // Controlled_Buffer controlled_buffer_1
endmodule

module isZero (
  input  [31:0] Input,
  output out_2
);

  wire or_1_out;

  or or_1 (or_1_out, Input[0], Input[1], Input[2], Input[3], Input[4], Input[5], Input[6], Input[7], Input[8], Input[9], Input[10], Input[11], Input[12], Input[13], Input[14], Input[15], Input[16], Input[17], Input[18], Input[19], Input[20], Input[21], Input[22], Input[23], Input[24], Input[25], Input[26], Input[27], Input[28], Input[29], Input[30], Input[31]);
  not not_1 (out_2, or_1_out);
endmodule

module Sign_Extend__TO_DO (
  input  [15:0] Input,
  output [31:0] Output
);


  assign Output = {{17{Input[15]}}, Input[14:0]};
endmodule

module Zero_Extension__TO_DO (
  input  [15:0] Input,
  output [31:0] Output
);


  assign Output = {{16{1'b0}}, Input};
endmodule

module Overflow_Detection__TO_DO (
  input  MSB_A,
  input  MSB_B,
  input  MSB_Result,
  output Overflow
);

  wire xnor_1_out, xor_1_out;

  xnor xnor_1 (xnor_1_out, MSB_A, MSB_B);
  xor xor_1 (xor_1_out, MSB_B, MSB_Result);
  and and_1 (Overflow, xnor_1_out, xor_1_out);
endmodule

// SL2
module Shift_Left_2__TO_DO (
  input  [31:0] Input,
  output [31:0] Output
);


  assign Output = {Input[29:0], 2'b00};
endmodule

module Shift_Left_2___2__TO_DO (
  input  [15:0] Input,
  output [17:0] Output
);


  assign Output = {Input, 2'b00};
endmodule

module _32_bit_ALU__TO_DO (
  input  [3:0] ALUOp,
  input  [31:0] a,
  input  [31:0] b,
  output Zero,
  output [31:0] Result
);

  wire not_3_out, Overflow_overflow;
  wire [30:0] adder_1_out, multiplexer_1_out, multiplexer_2_out;
  wire [31:0] and_1_out, not_1_out, not_2_out, or_1_out;
  wire [31:31] adder_1_out_2, multiplexer_1_out_2, multiplexer_2_out_2, multiplexer_3_out;

  assign not_1_out = ~a;  // NOT_Gate not_1, 32 bits wide
  Multiplexer #(.width(32), .enable("false")) multiplexer_1 (
    .in0(a), .in1(not_1_out), .out({multiplexer_1_out_2[31], multiplexer_1_out}), .sel(ALUOp[3]));
  Multiplexer #(.width(32), .enable("false")) multiplexer_2 (
    .in0(b), .in1(not_2_out), .out({multiplexer_2_out_2[31], multiplexer_2_out}), .sel(ALUOp[2]));
  assign not_2_out = ~b;  // NOT_Gate not_2, 32 bits wide
  Overflow_Detection__TO_DO Overflow (
    .MSB_A(multiplexer_1_out_2[31]), .MSB_B(multiplexer_2_out_2[31]), .MSB_Result(adder_1_out_2[31]),
    .Overflow(Overflow_overflow));
  not not_3 (not_3_out, adder_1_out_2[31]);
  Multiplexer #(.enable("false")) multiplexer_3 (
    .in0(adder_1_out_2[31]), .in1(not_3_out), .out(multiplexer_3_out[31]), .sel(Overflow_overflow));
  assign and_1_out = {multiplexer_1_out_2[31], multiplexer_1_out} & {multiplexer_2_out_2[31], multiplexer_2_out};  // AND_Gate and_1, 32 bits wide
  assign or_1_out = {multiplexer_1_out_2[31], multiplexer_1_out} | {multiplexer_2_out_2[31], multiplexer_2_out};  // OR_Gate or_1, 32 bits wide
  Adder #(.width(32)) adder_1 (
    .a({multiplexer_1_out_2[31], multiplexer_1_out}), .b({multiplexer_2_out_2[31], multiplexer_2_out}),
    .out({adder_1_out_2[31], adder_1_out}), .cin(ALUOp[2]));  // open: cout
  Multiplexer #(.select(2), .width(32), .enable("false")) multiplexer_4 (
    .in0(and_1_out), .in1(or_1_out), .in2({adder_1_out_2[31], adder_1_out}),
    .in3({multiplexer_3_out[31], {31{1'b0}}}), .out(Result), .sel(ALUOp[1:0]));
  isZero isZero (.Input(Result), .out_2(Zero));
endmodule

// ALU
module _32_bit_ALU_with_Shifts__TO_DO (
  input  [3:0] ALUOp,
  input  [31:0] a,
  input  [31:0] b,
  input  [4:0] shamt,
  input  [1:0] ShiftOp,
  output Zero,
  output [31:0] Result
);

  wire [31:0] n32_bit_alu_to_do_1_result, shifter_1_out, shifter_2_out;

  _32_bit_ALU__TO_DO u_32_bit_alu_to_do_1 (
    .a(a), .b(b), .ALUOp(ALUOp), .Zero(Zero), .Result(n32_bit_alu_to_do_1_result));
  Shifter #(.width(32)) shifter_1 (.in(b), .\dist (shamt), .out(shifter_1_out));
  Shifter #(.width(32), .shift("lr")) shifter_2 (.in(b), .\dist (shamt), .out(shifter_2_out));
  Multiplexer #(.select(2), .width(32), .enable("false")) multiplexer_1 (
    .in0(n32_bit_alu_to_do_1_result), .in2(shifter_1_out), .in3(shifter_2_out), .out(Result), .sel(ShiftOp));  // open: in1
endmodule

// Reg
module Register_File__TO_DO (
  input  [4:0] Read_register_1,
  input  RegWrite,
  input  [4:0] Read_register_2,
  input  Clock,
  input  Clear,
  input  [4:0] Write_register,
  input  [31:0] Write_data,
  input  [31:0] WriteTo_t9,
  input  WriteSignal,
  output [31:0] Read_data_1,
  output [31:0] Read_data_2,
  output [31:0] t8_to_LCD,
  output [31:0] t9_to_Keypad
);

  wire controlled_buffer_2_out, demultiplexer_1_out0, demultiplexer_1_out1, demultiplexer_1_out2,
       demultiplexer_1_out3, demultiplexer_1_out4, demultiplexer_1_out5, demultiplexer_1_out6,
       demultiplexer_1_out7, demultiplexer_1_out8, demultiplexer_1_out9, demultiplexer_1_out10,
       demultiplexer_1_out11, demultiplexer_1_out12, demultiplexer_1_out13, demultiplexer_1_out14,
       demultiplexer_1_out15, demultiplexer_1_out16, demultiplexer_1_out17, demultiplexer_1_out18,
       demultiplexer_1_out19, demultiplexer_1_out20, demultiplexer_1_out21, demultiplexer_1_out22,
       demultiplexer_1_out23, demultiplexer_1_out24, demultiplexer_1_out25, demultiplexer_1_out26,
       demultiplexer_1_out27, demultiplexer_1_out28, demultiplexer_1_out29, demultiplexer_1_out30,
       demultiplexer_1_out31;
  wire [31:0] _15_q, _31_q, controlled_buffer_1_out, register_1_q, register_2_q, register_3_q, register_4_q,
       register_5_q, register_6_q, register_7_q, register_8_q, register_9_q, register_10_q, register_11_q,
       register_12_q, register_13_q, register_14_q, register_15_q, register_16_q, register_17_q,
       register_18_q, register_19_q, register_20_q, register_21_q, register_22_q, register_23_q,
       register_24_q, register_25_q, register_26_q, register_27_q, register_28_q;

  assign controlled_buffer_1_out = WriteSignal ? WriteTo_t9 : 32'bz;  // Controlled_Buffer controlled_buffer_1
  assign controlled_buffer_2_out = WriteSignal ? WriteSignal : 1'bz;  // Controlled_Buffer controlled_buffer_2
  Demultiplexer #(.select(5), .enable("false")) demultiplexer_1 (
    .out0(demultiplexer_1_out0), .out1(demultiplexer_1_out1), .out2(demultiplexer_1_out2),
    .out3(demultiplexer_1_out3), .out4(demultiplexer_1_out4), .out5(demultiplexer_1_out5),
    .out6(demultiplexer_1_out6), .out7(demultiplexer_1_out7), .out8(demultiplexer_1_out8),
    .out9(demultiplexer_1_out9), .out10(demultiplexer_1_out10), .out11(demultiplexer_1_out11),
    .out12(demultiplexer_1_out12), .out13(demultiplexer_1_out13), .out14(demultiplexer_1_out14),
    .out15(demultiplexer_1_out15), .out16(demultiplexer_1_out16), .out17(demultiplexer_1_out17),
    .out18(demultiplexer_1_out18), .out19(demultiplexer_1_out19), .out20(demultiplexer_1_out20),
    .out21(demultiplexer_1_out21), .out22(demultiplexer_1_out22), .out23(demultiplexer_1_out23),
    .out24(demultiplexer_1_out24), .out25(demultiplexer_1_out25), .out26(demultiplexer_1_out26),
    .out27(demultiplexer_1_out27), .out28(demultiplexer_1_out28), .out29(demultiplexer_1_out29),
    .out30(demultiplexer_1_out30), .out31(demultiplexer_1_out31), .in(RegWrite), .sel(Write_register));
  assign controlled_buffer_1_out = demultiplexer_1_out25 ? Write_data : 32'bz;  // Controlled_Buffer controlled_buffer_3
  assign controlled_buffer_2_out = demultiplexer_1_out25 ? demultiplexer_1_out25 : 1'bz;  // Controlled_Buffer controlled_buffer_4
  Register #(.width(32), .trigger("falling")) register_1 (
    .D(Write_data), .en(demultiplexer_1_out0), .Q(register_1_q), .clk(Clock), .clr(Clear));
  Register #(.width(32), .trigger("falling")) register_2 (
    .D(Write_data), .en(demultiplexer_1_out1), .Q(register_2_q), .clk(Clock), .clr(Clear));
  Register #(.width(32), .trigger("falling")) register_3 (
    .D(Write_data), .en(demultiplexer_1_out2), .Q(register_3_q), .clk(Clock), .clr(Clear));
  Register #(.width(32), .trigger("falling")) register_4 (
    .D(Write_data), .en(demultiplexer_1_out3), .Q(register_4_q), .clk(Clock), .clr(Clear));
  Register #(.width(32), .trigger("falling")) register_5 (
    .D(Write_data), .en(demultiplexer_1_out4), .Q(register_5_q), .clk(Clock), .clr(Clear));
  Register #(.width(32), .trigger("falling")) register_6 (
    .D(Write_data), .en(demultiplexer_1_out5), .Q(register_6_q), .clk(Clock), .clr(Clear));
  Register #(.width(32), .trigger("falling")) register_7 (
    .D(Write_data), .en(demultiplexer_1_out6), .Q(register_7_q), .clk(Clock), .clr(Clear));
  Register #(.width(32), .trigger("falling")) register_8 (
    .D(Write_data), .en(demultiplexer_1_out7), .Q(register_8_q), .clk(Clock), .clr(Clear));
  Register #(.width(32), .trigger("falling")) register_9 (
    .D(Write_data), .en(demultiplexer_1_out8), .Q(register_9_q), .clk(Clock), .clr(Clear));
  Register #(.width(32), .trigger("falling")) register_10 (
    .D(Write_data), .en(demultiplexer_1_out9), .Q(register_10_q), .clk(Clock));  // open: clr
  Register #(.width(32), .trigger("falling")) register_11 (
    .D(Write_data), .en(demultiplexer_1_out10), .Q(register_11_q), .clk(Clock));  // open: clr
  Register #(.width(32), .trigger("falling")) register_12 (
    .D(Write_data), .en(demultiplexer_1_out11), .Q(register_12_q), .clk(Clock));  // open: clr
  Register #(.width(32), .trigger("falling")) register_13 (
    .D(Write_data), .en(demultiplexer_1_out12), .Q(register_13_q), .clk(Clock));  // open: clr
  Register #(.width(32), .trigger("falling")) register_14 (
    .D(Write_data), .en(demultiplexer_1_out13), .Q(register_14_q), .clk(Clock));  // open: clr
  Register #(.width(32), .trigger("falling")) register_15 (
    .D(Write_data), .en(demultiplexer_1_out14), .Q(register_15_q), .clk(Clock));  // open: clr
  Register #(.width(32), .trigger("falling")) _15 (
    .D(Write_data), .en(demultiplexer_1_out15), .Q(_15_q), .clk(Clock), .clr(Clear));
  Register #(.width(32), .trigger("falling")) register_16 (
    .D(Write_data), .en(demultiplexer_1_out16), .Q(register_16_q), .clk(Clock), .clr(Clear));
  Register #(.width(32), .trigger("falling")) register_17 (
    .D(Write_data), .en(demultiplexer_1_out17), .Q(register_17_q), .clk(Clock), .clr(Clear));
  Register #(.width(32), .trigger("falling")) register_18 (
    .D(Write_data), .en(demultiplexer_1_out18), .Q(register_18_q), .clk(Clock), .clr(Clear));
  Register #(.width(32), .trigger("falling")) register_19 (
    .D(Write_data), .en(demultiplexer_1_out19), .Q(register_19_q), .clk(Clock), .clr(Clear));
  Register #(.width(32), .trigger("falling")) register_20 (
    .D(Write_data), .en(demultiplexer_1_out20), .Q(register_20_q), .clk(Clock), .clr(Clear));
  Register #(.width(32), .trigger("falling")) register_21 (
    .D(Write_data), .en(demultiplexer_1_out21), .Q(register_21_q), .clk(Clock), .clr(Clear));
  Register #(.width(32), .trigger("falling")) register_22 (
    .D(Write_data), .en(demultiplexer_1_out22), .Q(register_22_q), .clk(Clock), .clr(Clear));
  Register #(.width(32), .trigger("falling")) register_23 (
    .D(Write_data), .en(demultiplexer_1_out23), .Q(register_23_q), .clk(Clock), .clr(Clear));
  Register #(.width(32), .trigger("falling")) _24 (
    .D(Write_data), .en(demultiplexer_1_out24), .Q(t8_to_LCD), .clk(Clock), .clr(Clear));
  Register #(.width(32), .trigger("falling")) _25 (
    .D(controlled_buffer_1_out), .en(controlled_buffer_2_out), .Q(t9_to_Keypad), .clk(Clock), .clr(Clear));
  Register #(.width(32), .trigger("falling")) register_24 (
    .en(demultiplexer_1_out26), .Q(register_24_q), .clk(Clock), .clr(Clear));  // open: D
  Register #(.width(32), .trigger("falling")) register_25 (
    .D(Write_data), .en(demultiplexer_1_out27), .Q(register_25_q), .clk(Clock), .clr(Clear));
  Register #(.width(32), .trigger("falling")) register_26 (
    .D(Write_data), .en(demultiplexer_1_out28), .Q(register_26_q), .clk(Clock), .clr(Clear));
  Register #(.width(32), .trigger("falling")) register_27 (
    .D(Write_data), .en(demultiplexer_1_out29), .Q(register_27_q), .clk(Clock), .clr(Clear));
  Register #(.width(32), .trigger("falling")) register_28 (
    .D(Write_data), .en(demultiplexer_1_out30), .Q(register_28_q), .clk(Clock), .clr(Clear));
  Register #(.width(32), .trigger("falling")) _31 (
    .D(Write_data), .en(demultiplexer_1_out31), .Q(_31_q), .clk(Clock), .clr(Clear));
  Multiplexer #(.select(5), .width(32), .enable("false")) multiplexer_1 (
    .in0(register_1_q), .in1(register_2_q), .in2(register_3_q), .in3(register_4_q), .in4(register_5_q),
    .in5(register_6_q), .in6(register_7_q), .in7(register_8_q), .in8(register_9_q), .in9(register_10_q),
    .in10(register_11_q), .in11(register_12_q), .in12(register_13_q), .in13(register_14_q),
    .in14(register_15_q), .in15(_15_q), .in16(register_16_q), .in17(register_17_q), .in18(register_18_q),
    .in19(register_19_q), .in20(register_20_q), .in21(register_21_q), .in22(register_22_q),
    .in23(register_23_q), .in24(t8_to_LCD), .in25(t9_to_Keypad), .in26(register_24_q), .in27(register_25_q),
    .in28(register_26_q), .in29(register_27_q), .in30(register_28_q), .in31(_31_q), .out(Read_data_1),
    .sel(Read_register_1));
  Multiplexer #(.select(5), .width(32), .enable("false")) multiplexer_2 (
    .in0(register_1_q), .in1(register_2_q), .in2(register_3_q), .in3(register_4_q), .in4(register_5_q),
    .in5(register_6_q), .in6(register_7_q), .in7(register_8_q), .in8(register_9_q), .in9(register_10_q),
    .in10(register_11_q), .in11(register_12_q), .in12(register_13_q), .in13(register_14_q),
    .in14(register_15_q), .in15(_15_q), .in16(register_16_q), .in17(register_17_q), .in18(register_18_q),
    .in19(register_19_q), .in20(register_20_q), .in21(register_21_q), .in22(register_22_q),
    .in23(register_23_q), .in24(t8_to_LCD), .in25(t9_to_Keypad), .in26(register_24_q), .in27(register_25_q),
    .in28(register_26_q), .in29(register_27_q), .in30(register_28_q), .in31(_31_q), .out(Read_data_2),
    .sel(Read_register_2));
endmodule

// Mem
module Instruction_Memory__TO_DO (
  input  [31:0] PC,
  output [31:0] Instruction
);

  ROM #(.addrWidth(16), .dataWidth(32)) rom_1 (.addr(PC[17:2]), .data(Instruction));  // open: sel

  // Notes on the sheet:
  //   contents of rom_1 (hex, n*v repeats v):
  //   c020 c820 8020 8820 9020 1320ffff 194040 84042 2909000a 11200007 1048c0 1304820 1308020 2088020
  //   10c020 c820 8100005 2009000f 1109ffed 2009000e 11090012 89020 c820 1320ffff 194040 84042 2909000a
  //   11200007 1148c0 1314820 1318820 2288820 11c020 c820 8100017 2009000f 1109ffdb 2009000e 11090000
  //   16400003 10c020 c820 8100059 2008000a 12480007 2008000b 12480008 2008000c 12480009 2008000d 12480014
  //   8100000 211c020 c820 8100059 211c022 c820 8100059 104020 114820 5020 11200006 312b0001 11600001
  //   1485020 84040 94842 810003d 140c020 c820 8100059 104020 114c00 5020 200b0011 1160000a 109602a
  //   15800004 1094022 a5040 354a0001 8100053 a5040 94842 216bffff 810004b 140c020 c820 8100059 1320ffff
  //   194040 84042 2009000f 1109ffa2 c820 8100059
endmodule

// CU
module Control_Unit__TO_DO (
  input  [5:0] Opcode,
  input  [5:0] Funct,
  output ALUSrc,
  output [3:0] ALUOp,
  output RegDst,
  output RegWrite,
  output [1:0] SHFTOp,
  output invZero,
  output Branch,
  output Jump
);

  wire add_out, addi_out, and_out, andi_out, beq_out, bne_out, nor_out, not_1_out, not_2_out, not_3_out,
       not_4_out, not_5_out, not_6_out, not_8_out, not_9_out, not_10_out, not_11_out, not_12_out, not_13_out,
       or_1_out, or_2_out, ori_out, sll_out, slt_out, slti_out, srl_out, sub_out;
  wire [1:0] and_2_out;

  not not_1 (not_1_out, Opcode[5]);
  not not_2 (not_2_out, Opcode[3]);
  not not_3 (not_3_out, Opcode[2]);
  not not_4 (not_4_out, Opcode[4]);
  not not_5 (not_5_out, Opcode[1]);
  or or_1 (or_1_out, Opcode[0], Opcode[1], Opcode[2], Opcode[3], Opcode[4], Opcode[5]);
  not not_6 (not_6_out, Opcode[0]);
  not not_7 (and_2_out[1], or_1_out);
  not not_8 (not_8_out, Funct[5]);
  not not_9 (not_9_out, Funct[4]);
  not not_10 (not_10_out, Funct[3]);
  not not_11 (not_11_out, Funct[1]);
  not not_12 (not_12_out, Funct[2]);
  not not_13 (not_13_out, Funct[0]);
  ALUOp_Generator ALUOp_Gen (
    .Funct5(Funct[5]), .Funct3(Funct[3]), .Funct2(Funct[2]), .Funct1(Funct[1]), .Funct0(Funct[0]),
    .Op3(Opcode[3]), .Op2(Opcode[2]), .Op1(Opcode[1]), .Op0(Opcode[0]), .ALUOP3(ALUOp[3]), .ALUOP2(ALUOp[2]),
    .ALUOP1(ALUOp[1]), .ALUOP0(ALUOp[0]));
  and add (add_out, not_13_out, not_11_out, not_12_out, not_10_out, not_9_out, Funct[5], and_2_out[1]);
  and \and  (and_out, not_13_out, not_11_out, Funct[2], not_10_out, not_9_out, Funct[5], and_2_out[1]);
  and sub (sub_out, not_13_out, Funct[1], not_12_out, not_10_out, not_9_out, Funct[5], and_2_out[1]);
  and or_2 (or_2_out, Funct[0], not_11_out, Funct[2], not_10_out, not_9_out, Funct[5], and_2_out[1]);
  and \nor  (nor_out, Funct[0], Funct[1], Funct[2], not_10_out, not_9_out, Funct[5], and_2_out[1]);
  and slt (slt_out, not_13_out, Funct[1], not_12_out, Funct[3], not_9_out, Funct[5], and_2_out[1]);
  and sll (sll_out, not_13_out, not_11_out, not_12_out, not_10_out, not_9_out, not_8_out, and_2_out[1]);
  and addi (addi_out, not_6_out, not_5_out, not_3_out, Opcode[3], not_4_out, not_1_out);
  and andi (andi_out, not_6_out, not_5_out, Opcode[2], Opcode[3], not_4_out, not_1_out);
  and ori (ori_out, Opcode[0], not_5_out, Opcode[2], Opcode[3], not_4_out, not_1_out);
  and slti (slti_out, not_6_out, Opcode[1], not_3_out, Opcode[3], not_4_out, not_1_out);
  and beq (beq_out, not_6_out, not_5_out, Opcode[2], not_2_out, not_4_out, not_1_out);
  and bne (bne_out, Opcode[0], not_5_out, Opcode[2], not_2_out, not_4_out, not_1_out);
  and j (Jump, not_6_out, Opcode[1], not_3_out, not_2_out, not_4_out, not_1_out);
  and srl (srl_out, not_13_out, Funct[1], not_12_out, not_10_out, not_9_out, not_8_out, and_2_out[1]);
  or or_3 (RegDst, add_out, and_out, sub_out, or_2_out, nor_out, slt_out, sll_out, srl_out);
  or or_4 (RegWrite, add_out, and_out, sub_out, or_2_out, nor_out, slt_out, sll_out, srl_out, addi_out, andi_out, ori_out, slti_out);
  and and_2 (and_2_out[0], and_2_out[1], Funct[1]);
  or or_5 (Branch, beq_out, bne_out);
  Multiplexer #(.width(2), .enable("false")) multiplexer_1 (
    .in0(2'b00), .in1(and_2_out), .out(SHFTOp), .sel(and_2_out[1]));
  and and_3 (invZero, Opcode[0], Branch);

  assign ALUSrc = Opcode[3];
endmodule

module CPU__TO_DO (
  input  Clock,
  input  Clear,
  input  WriteSig,
  input  [31:0] WriteTo_t9,
  output [31:0] t8ToLCD,
  output [31:0] t9ToKeypad
);

  wire and_1_out, control_unit_to_do_1_alusrc, control_unit_to_do_1_branch, control_unit_to_do_1_invzero,
       control_unit_to_do_1_jump, control_unit_to_do_1_regdst, control_unit_to_do_1_regwrite,
       n32_bit_alu_with_shifts_to_do_1_zero, xnor_1_out;
  wire [1:0] control_unit_to_do_1_shftop;
  wire [3:0] control_unit_to_do_1_aluop;
  wire [4:0] multiplexer_1_out;
  wire [31:0] adder_1_out, adder_2_out, instruction_memory_to_do_1_instruction, multiplexer_2_out,
       multiplexer_3_out, multiplexer_4_out, n32_bit_alu_with_shifts_to_do_1_result, PC_q,
       register_file_to_do_1_read_data_1, register_file_to_do_1_read_data_2, shift_left_2_to_do_1_output,
       Sign_extend_output;

  Register #(.width(32), .trigger("falling")) PC (
    .D(multiplexer_2_out), .Q(PC_q), .clk(Clock), .clr(Clear));  // open: en
  Instruction_Memory__TO_DO instruction_memory_to_do_1 (
    .PC(PC_q), .Instruction(instruction_memory_to_do_1_instruction));
  Adder #(.width(32)) adder_1 (.a(32'h4), .b(PC_q), .out(adder_1_out));  // open: cin, cout
  Multiplexer #(.width(5), .enable("false")) multiplexer_1 (
    .in0(instruction_memory_to_do_1_instruction[20:16]), .in1(instruction_memory_to_do_1_instruction[15:11]),
    .out(multiplexer_1_out), .sel(control_unit_to_do_1_regdst));
  Sign_Extend__TO_DO Sign_extend (.Input(instruction_memory_to_do_1_instruction[15:0]), .Output(Sign_extend_output));
  Shift_Left_2__TO_DO shift_left_2_to_do_1 (.Input(Sign_extend_output), .Output(shift_left_2_to_do_1_output));
  Control_Unit__TO_DO control_unit_to_do_1 (
    .Opcode(instruction_memory_to_do_1_instruction[31:26]),
    .Funct(instruction_memory_to_do_1_instruction[5:0]), .ALUSrc(control_unit_to_do_1_alusrc),
    .ALUOp(control_unit_to_do_1_aluop), .RegDst(control_unit_to_do_1_regdst),
    .RegWrite(control_unit_to_do_1_regwrite), .SHFTOp(control_unit_to_do_1_shftop),
    .invZero(control_unit_to_do_1_invzero), .Branch(control_unit_to_do_1_branch),
    .Jump(control_unit_to_do_1_jump));
  Adder #(.width(32)) adder_2 (.a(adder_1_out), .b(shift_left_2_to_do_1_output), .out(adder_2_out));  // open: cin, cout
  Multiplexer #(.width(32), .enable("false")) multiplexer_2 (
    .in0({adder_1_out[31:28], instruction_memory_to_do_1_instruction[25:0], 2'b00}), .in1(multiplexer_3_out),
    .out(multiplexer_2_out), .sel(control_unit_to_do_1_jump));
  Register_File__TO_DO register_file_to_do_1 (
    .Write_data(n32_bit_alu_with_shifts_to_do_1_result), .RegWrite(control_unit_to_do_1_regwrite),
    .Write_register(multiplexer_1_out), .Read_register_2(instruction_memory_to_do_1_instruction[20:16]),
    .Read_data_2(register_file_to_do_1_read_data_2),
    .Read_register_1(instruction_memory_to_do_1_instruction[25:21]),
    .Read_data_1(register_file_to_do_1_read_data_1), .Clock(Clock), .WriteTo_t9(WriteTo_t9),
    .WriteSignal(WriteSig), .t9_to_Keypad(t9ToKeypad), .t8_to_LCD(t8ToLCD), .Clear(Clear));
  Multiplexer #(.width(32), .enable("false")) multiplexer_3 (
    .in0(adder_1_out), .in1(adder_2_out), .out(multiplexer_3_out), .sel(and_1_out));
  _32_bit_ALU_with_Shifts__TO_DO u_32_bit_alu_with_shifts_to_do_1 (
    .a(register_file_to_do_1_read_data_1), .b(multiplexer_4_out),
    .shamt(instruction_memory_to_do_1_instruction[10:6]), .ALUOp(control_unit_to_do_1_aluop),
    .ShiftOp(control_unit_to_do_1_shftop), .Zero(n32_bit_alu_with_shifts_to_do_1_zero),
    .Result(n32_bit_alu_with_shifts_to_do_1_result));
  Multiplexer #(.width(32), .enable("false")) multiplexer_4 (
    .in0(register_file_to_do_1_read_data_2), .in1(Sign_extend_output), .out(multiplexer_4_out),
    .sel(control_unit_to_do_1_alusrc));
  xnor xnor_1 (xnor_1_out, control_unit_to_do_1_invzero, n32_bit_alu_with_shifts_to_do_1_zero);
  and and_1 (and_1_out, control_unit_to_do_1_branch, xnor_1_out);

  // Notes on the sheet:
  //   op
  //   rs
  //   funct
  //   imm
  //   rt
  //   rd
  //   shamt
endmodule

module ALUOp_Generator (
  input  Op3,
  input  Op2,
  input  Op1,
  input  Op0,
  input  Funct5,
  input  Funct3,
  input  Funct2,
  input  Funct1,
  input  Funct0,
  output ALUOP3,
  output ALUOP2,
  output ALUOP1,
  output ALUOP0
);

  wire and_1_out, and_2_out, and_3_out, and_4_out, and_5_out, and_6_out, and_7_out, and_8_out, and_9_out,
       and_10_out, not_1_out, not_2_out, not_3_out, not_4_out, not_5_out, not_6_out, not_7_out, not_8_out,
       not_9_out, not_10_out, not_11_out, not_12_out, not_13_out;

  not not_1 (not_1_out, Op3);
  not not_2 (not_2_out, Op2);
  not not_3 (not_3_out, Op3);
  not not_4 (not_4_out, Op3);
  not not_5 (not_5_out, Op3);
  not not_6 (not_6_out, Funct2);
  not not_7 (not_7_out, Op3);
  not not_8 (not_8_out, Op2);
  not not_9 (not_9_out, Op3);
  not not_10 (not_10_out, Op2);
  not not_11 (not_11_out, Funct1);
  not not_12 (not_12_out, Op3);
  not not_13 (not_13_out, Op2);
  and and_1 (and_1_out, not_1_out, not_2_out, Funct2, Funct1);
  and and_2 (and_2_out, Op1, Funct5, Funct3, Funct2, Funct1, Funct0);
  and and_3 (and_3_out, not_3_out, Funct1);
  and and_4 (and_4_out, not_4_out, Op2);
  and and_5 (and_5_out, not_5_out, not_6_out);
  and and_6 (and_6_out, not_7_out, Op2);
  and and_7 (and_7_out, Op3, not_8_out);
  and and_8 (and_8_out, not_9_out, not_10_out, not_11_out, Funct0);
  and and_9 (and_9_out, not_12_out, not_13_out, Funct3);
  and and_10 (and_10_out, Op3, Op0);
  or or_1 (ALUOP3, and_1_out, and_2_out);
  or or_2 (ALUOP2, and_3_out, Op1, and_4_out);
  or or_3 (ALUOP1, and_5_out, and_6_out, and_7_out);
  or or_4 (ALUOP0, and_8_out, and_9_out, Op1, and_10_out);
endmodule
